# Fritzing sketch Proyek_Mini (saved by Fritzing 0.9.3b)
breadboards: 1

parts:
  Part1 = MQ-3 breakout
  Part2 = Arduino Uno (Rev3) - ICSP
  LED1 = LED - 3mm [color="Red (633nm)" package="3 mm [THT]"]
  J1 = Piezo Speaker
  R1 = Resistor [tolerance=±5% resistance=220 package="0603 [SMD]"]
  Display1 = LCD screen 16x2 IIC [part_number=101290]

nets:
  VCC: Part1.VCC, Part2.5V, Display1.VCC
  GND: Part1.GND, Part2.GND, LED1.cathode, J1.pin1, Display1.GND
  N1: Part1.AO, Part2.A0
  N2: Part2.A4/SDA, Display1.SDA
  N3: Part2.A5/SCL, Display1.SCL
  N4: Part2.D4, R1.Pin_0
  N5: Part2.D5_PWM, J1.pin2
  N6: LED1.anode, R1.Pin_1

custom parts:
  MQ-3 breakout: Alcohol sensor is capable of detecting alcohol (ethanol) particles on itself and gives the information in digital form back to us to manipulate with it. SKU:101251 • Voltage: 5V DC • Power: max 750mW • Measurement range: 0.04-4mg/L
  LCD screen 16x2 IIC: LCD screen with HD44780 controller enables showing text, symbols, value or anything else that comes from Croduino/Arduino. It is capable of showing 16 symbols in two lines and therefore can be used in many projects that need to send clearly visible and legible output information.. • Color of symbols: White • Backlight: Blue • Dimensions: 80 x 36 x 12 mm • Screen dimensions: 64.5 x 16 mm •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
