# Fritzing sketch Tugas1 (saved by Fritzing 0.9.3b)
breadboards: 1

parts:
  U1 = NodeMCU V1.0
  LED1 = LED - 5mm [color="Red (633nm)" package="5 mm [THT]"]
  LED2 = LED - 5mm [color="Yellow (585nm)" package="5 mm [THT]"]
  LED3 = LED - 5mm [color="Green (555nm)" package="5 mm [THT]"]
  R1 = Resistor [tolerance=±5% resistance=220 package=THT]
  R2 = Resistor [tolerance=±5% resistance=220 package=THT]
  R3 = Resistor [tolerance=±5% resistance=220 package=THT]

nets:
  N1: U1.D1, R1.Pin_0
  N2: U1.D2, R2.Pin_0
  N3: U1.D3, R3.Pin_0
  N4: U1.GND, LED1.cathode, LED2.cathode, LED3.cathode
  N5: LED1.anode, R1.Pin_1
  N6: LED2.anode, R2.Pin_1
  N7: LED3.anode, R3.Pin_1

custom parts:
  NodeMCU V1.0: ESP8266 based NodeMCU
